# Fritzing sketch 003_Board (saved by Fritzing 0.9.5d)
breadboards: 1

parts:
  R1 = Rotary Potentiometer (Large) [maximum_resistance=100kΩ package=THT]
  A1 = devebox 32f407vgt6
  R2 = Resistor [tolerance=±5% resistance=5.1k package=THT]

nets:
  N1: R1.leg1, R2.Pin_1
  N2: R1.wiper, A1.Pin_72
  N3: R1.leg2, A1.Pin_2, A1.Pin_100
  N4: A1.Pin_1, R2.Pin_0

custom parts:
  devebox 32f407vgt6: Devebox 32f407vgt6 develpment board.
